# Fritzing sketch Smart Room Controller FRITZ (saved by Fritzing 0.9.4)
breadboards: 3

parts:
  Teensy_3_1 = Teensy 3.1
  M1 = BMP280
  OLED_I2C1 = OLED 128x64 I2C Monochrome Display
  WS2812B1 = WS2812B [package="DIP (Dual Inline) [THT]"]
  WS2812B2 = WS2812B [package="DIP (Dual Inline) [THT]"]
  WS2812B3 = WS2812B [package="DIP (Dual Inline) [THT]"]
  WS2812B4 = WS2812B [package="DIP (Dual Inline) [THT]"]
  J1 = Basic Servo
  RG_encoder1 = SprkFn RG Encoder [package="DIP (Dual Inline) [THT]"]
  Part1 = Thumb Joystick
  WIZ820io1 = WIZ820io [part_number=WIZ820io]

nets (from the schematic view):
  GND: Teensy_3_1.GND, M1.GND, OLED_I2C1.GND, WS2812B1.GND, WS2812B2.GND, WS2812B3.GND, WS2812B4.GND, J1.gnd, RG_encoder1.B, Part1.GND, WIZ820io1.GND
  N1: Teensy_3_1.D1, WIZ820io1.nRESET
  N2: Teensy_3_1.D2, Part1.SEL
  N3: Teensy_3_1.D5, J1.pulse
  N4: Teensy_3_1.D7, RG_encoder1.A
  N5: Teensy_3_1.D8, RG_encoder1.C
  N6: Teensy_3_1.D10, WIZ820io1.nSS
  N7: Teensy_3_1.D11, WIZ820io1.MOSI
  N8: Teensy_3_1.D12, WIZ820io1.MISO
  N9: Teensy_3_1.D13, WIZ820io1.SCLK
  N10: Teensy_3_1.A0/D14, Part1.HORZ
  N11: Teensy_3_1.A1/D15, Part1.VERT
  N12: Teensy_3_1.A3/D17, WS2812B1.DI
  N13: Teensy_3_1.A4/D18, M1.SDA, OLED_I2C1.SDA
  N14: Teensy_3_1.A5/D19, M1.SCL, OLED_I2C1.SCK
  5V: Teensy_3_1.3V3, M1.VIN, OLED_I2C1.VDD, WS2812B1.5V, WS2812B2.5V, WS2812B3.5V, WS2812B4.5V, J1.vcc, Part1.VCC, WIZ820io1.VIN
  N15: WS2812B1.DO, WS2812B2.DI
  N16: WS2812B2.DO, WS2812B3.DI
  N17: WS2812B3.DO, WS2812B4.DI

custom parts:
  BMP280: Temperature Humidity Barometric presure Sensor, I2C
  WS2812B: Adafruit NeoPixel Breakout
  SprkFn RG Encoder: SparkFun RG Rotary Encoder
